# Fritzing sketch hardware (saved by Fritzing 0.9.3b)
circuit board: 8.46667cm x 5.64444cm
breadboards: 1

parts:
  Part1 = Adafruit VCNL4010 Proximity and Light sensor [part_number="Adafruit #466"]
  M1 = STM32F103C8T6 blue mini board
  R1 = Resistor [tolerance=±5% resistance=220 package="2512 [SMD]"]
  LED1 = smd LED [color="Red (633nm)" package="1206 [SMD]"]
  BATT1 = 3xAAA Switchable Battery Pack w/JST connector

nets:
  N1: Part1.INT, M1.A0
  N2: Part1.SDA, M1.B7
  N3: Part1.SCL, M1.B6
  GND: Part1.GND, M1.G, M1.GND, R1.Pin_1, BATT1.NEG
  VIN: Part1.VIN, M1.5V, BATT1.POS
  N4: M1.A1, LED1.cathode
  N5: R1.Pin_0, LED1.anode

custom parts:
  Adafruit VCNL4010 Proximity and Light sensor: The VCNL4010 sensor is a nice way to add a small-distance proximity sensor to your microcontroller project. For longer distances (in the range of cm, you can use a SHARP IR distance sensor, but those are only good if the object is over 10 cm away. The VCNL4010 is designed for much shorter distances, no more than 200mm (about 7.5") and under our experimentation we found it worked best at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
  3xAAA Switchable Battery Pack w/JST connector: 3xAAA Switchable Battery Pack with JST connector
